# Fritzing sketch scheme-fritzing (saved by Fritzing 0.9.0b)

parts:
  U1 = NodeMCU V3.0
  U2 = WS2812 RGB LED matrix 8x8
  Часть1 = Real Time Clock Module - DS1307 RTC Breakout Board
  U3 = RF-LINK_RX [package=rf-link_rx]
  Power_plug1 = Power plug

nets:
  N1: U1.D0, U1.D1, Часть1.SDA
  N2: U1.D2, Часть1.SCL
  3V3: U1.3V3, Часть1.5V, U3.+5V
  GND: U1.GND, U1.D5, U1.RST, U2.GND, U2.DIN, Часть1.GND, U3.GND, Power_plug1.GND
  N3: U1.D6, U3.DATA
  VCC: U1.Vin, U2.VCC, Power_plug1.VCC

custom parts:
  NodeMCU V3.0: ESP8266 based NodeMCU
  WS2812 RGB LED matrix 8x8: WS2812 matrix 8x8
  RF-LINK_RX: RF Link receivers- WRL-8947, 8948, 8949, 8950
